# Fritzing sketch drv8825 (saved by Fritzing 0.9.3b)
breadboards: 1

parts:
  Bauteil1 = Arduino Uno (Rev3) - ICSP  # not connected
  DRV_1 = DRV 8825 Stepper Motor Carrier, High Current [part_number="DRV 8825"]  # not connected
  M1 = Stepper Motor - Bipolar  # not connected
  Power_plug1 = Power plug
  C1 = Electrolytic Capacitor [capacitance=100μF package="0807 [SMD, electrolytic]"]

nets:
  N1: Power_plug1.VCC, C1.+
  N2: Power_plug1.GND, C1.-
