# Fritzing sketch drv8825_mega_bak (saved by Fritzing 0.9.3b)
circuit board: 10.5cm x 7cm
breadboards: 12

parts:
  M1 = Stepper Motor - Bipolar
  SERVOS = Basic Servo
  S2 = Basic Servo
  S3 = Basic Servo
  S4 = Basic Servo
  5_4_3_2_1 = Basic Servo
  C1 = Capacitor Polarized [package=cpol-radial-100uf-25v]
  MEGA = Arduino Mega 2560 (Rev3)
  12V = screw terminal, 4 pins
  GND = screw terminal, 4 pins
  MICROSWITCHES = female pin header, 2 pins [form="♀ (female)"]
  MICRO2 = female pin header, 2 pins [form="♀ (female)"]
  MICRO3 = female pin header, 2 pins [form="♀ (female)"]
  MICRO4 = female pin header, 2 pins [form="♀ (female)"]
  MICRO5 = female pin header, 2 pins [form="♀ (female)"]
  SERVOS_2 = Basic Servo
  10_9_8_7_6 = Basic Servo
  S9 = Basic Servo
  S8 = Basic Servo
  S7 = Basic Servo
  RECEIVER = female pin header, 4 pins [form="♀ (female)"]
  D1 = Diode [package=diode-1n4001]
  R1 = Resistor [tolerance=±5% resistance=10k package=THT]
  DC1 = female pin header, 2 pins [form="♀ (female)"]
  D2 = Diode [package=diode-1n4001]
  R2 = Resistor [tolerance=±5% resistance=10k package=THT]
  DC2 = female pin header, 2 pins [form="♀ (female)"]
  FET1 = Basic FET N-Channel [package="TO220 [THT]"]
  FET2 = Basic FET N-Channel [package="TO220 [THT]"]
  SOCKET1 = female pin header, 8 pins [form="♀ (female)"]
  SOCKET1_2 = female pin header, 8 pins [form="♀ (female)"]
  SOCKET2 = female pin header, 8 pins [form="♀ (female)"]
  SOCKET2_2 = female pin header, 8 pins [form="♀ (female)"]
  M2 = Stepper Motor - Bipolar
  C2 = Capacitor Polarized [package=cpol-radial-100uf-25v]
  SOCKET3 = female pin header, 8 pins [form="♀ (female)"]
  SOCKET3_2 = female pin header, 8 pins [form="♀ (female)"]
  M3 = Stepper Motor - Bipolar
  C3 = Capacitor Polarized [package=cpol-radial-100uf-25v]
  SOCKET4 = female pin header, 8 pins [form="♀ (female)"]
  SOCKET4_2 = female pin header, 8 pins [form="♀ (female)"]
  M4 = Stepper Motor - Bipolar
  C4 = Capacitor Polarized [package=cpol-radial-100uf-25v]
  SOCKET5 = female pin header, 8 pins [form="♀ (female)"]
  SOCKET5_2 = female pin header, 8 pins [form="♀ (female)"]
  M5 = Stepper Motor - Bipolar
  C5 = Capacitor Polarized [package=cpol-radial-100uf-25v]
  5V = Screw terminal - 2 pins [package=THT]

nets:
  N1: M1.A, SOCKET1.pin3
  N2: M1.C, SOCKET1.pin4
  N3: M1.B, SOCKET1.pin5
  N4: M1.D, SOCKET1.pin6
  GND: SERVOS.gnd, S2.gnd, S3.gnd, S4.gnd, 5_4_3_2_1.gnd, C1.-, MEGA.GND, GND.pin1, GND.pin2, GND.pin3, GND.pin4, MICROSWITCHES.pin1, MICRO2.pin1, MICRO3.pin1, MICRO4.pin1, MICRO5.pin1, SERVOS_2.gnd, 10_9_8_7_6.gnd, S9.gnd, S8.gnd, S7.gnd, RECEIVER.pin4, R1.Pin_1, R2.Pin_1, FET1.source, FET2.source, SOCKET1.pin1, SOCKET1.pin7, SOCKET2.pin1, SOCKET2.pin7, C2.-, SOCKET3_2.pin1, SOCKET3_2.pin7, C3.-, SOCKET4_2.pin1, SOCKET4_2.pin7, C4.-, SOCKET5_2.pin1, SOCKET5_2.pin7, C5.-, 5V.pin2
  VCC: SERVOS.vcc, S2.vcc, S3.vcc, S4.vcc, 5_4_3_2_1.vcc, MEGA.5V, SERVOS_2.vcc, 10_9_8_7_6.vcc, S9.vcc, S8.vcc, S7.vcc, RECEIVER.pin1, SOCKET1_2.pin3, SOCKET1_2.pin4, SOCKET1_2.pin7, SOCKET2_2.pin3, SOCKET2_2.pin4, SOCKET2_2.pin7, SOCKET3.pin3, SOCKET3.pin4, SOCKET3.pin7, SOCKET4.pin3, SOCKET4.pin4, SOCKET4.pin7, SOCKET5.pin3, SOCKET5.pin4, SOCKET5.pin7, 5V.pin1
  N5: SERVOS.pulse, MEGA.D3_PWM
  N6: S2.pulse, MEGA.D4_PWM
  N7: S3.pulse, MEGA.D5_PWM
  N8: S4.pulse, MEGA.D6_PWM
  N9: 5_4_3_2_1.pulse, MEGA.D7_PWM
  N10: C1.+, 12V.pin1, 12V.pin2, 12V.pin3, 12V.pin4, D1.C, DC1.pin1, D2.C, DC2.pin1, SOCKET1.pin8, SOCKET4_2.pin8, C4.+
  N11: MEGA.A0, MICROSWITCHES.pin2
  N12: MEGA.A1, MICRO2.pin2
  N13: MEGA.A2, MICRO3.pin2
  N14: MEGA.A3, MICRO4.pin2
  N15: MEGA.A4, MICRO5.pin2
  N16: MEGA.D21/SCL, MEGA.SCL, SOCKET2_2.pin1
  N17: MEGA.D20/SDA, MEGA.SDA, SOCKET2_2.pin2
  N18: MEGA.D19/RX1, SOCKET2_2.pin5
  N19: MEGA.D18/TX1, SOCKET2_2.pin8
  N20: MEGA.D17_PWM/RX2, SOCKET1_2.pin1
  N21: MEGA.D16_PWM/TX2, SOCKET1_2.pin2
  N22: MEGA.D15/RX3, SOCKET1_2.pin5
  N23: MEGA.D14/TX3, SOCKET1_2.pin8
  N24: MEGA.D13_PWM, R2.Pin_0, FET2.gate
  N25: MEGA.D12_PWM, 10_9_8_7_6.pulse
  N26: MEGA.D11_PWM, S9.pulse
  N27: MEGA.D10_PWM, S8.pulse
  N28: MEGA.D9_PWM, S7.pulse
  N29: MEGA.D8_PWM, SERVOS_2.pulse
  N30: MEGA.D2_PWM, R1.Pin_0, FET1.gate
  N31: MEGA.D22, SOCKET3.pin8
  N32: MEGA.D24, SOCKET3.pin5
  N33: MEGA.D26, SOCKET3.pin2
  N34: MEGA.D28, SOCKET3.pin1
  N35: MEGA.D30, SOCKET4.pin8
  N36: MEGA.D32, SOCKET4.pin5
  N37: MEGA.D34, SOCKET4.pin2
  N38: MEGA.D36, SOCKET4.pin1
  N39: MEGA.D42, SOCKET5.pin8
  N40: MEGA.D44, SOCKET5.pin5
  N41: MEGA.D46, SOCKET5.pin2
  N42: MEGA.D48, SOCKET5.pin1
  N43: MEGA.D52, RECEIVER.pin2
  N44: D1.A, DC1.pin2, FET1.drain
  N45: D2.A, DC2.pin2, FET2.drain
  N46: SOCKET2.pin3, M2.A
  N47: SOCKET2.pin4, M2.C
  N48: SOCKET2.pin5, M2.B
  N49: SOCKET2.pin6, M2.D
  N50: SOCKET2.pin8, C2.+
  N51: SOCKET3_2.pin3, M3.A
  N52: SOCKET3_2.pin4, M3.C
  N53: SOCKET3_2.pin5, M3.B
  N54: SOCKET3_2.pin6, M3.D
  N55: SOCKET3_2.pin8, C3.+
  N56: SOCKET4_2.pin3, M4.A
  N57: SOCKET4_2.pin4, M4.C
  N58: SOCKET4_2.pin5, M4.B
  N59: SOCKET4_2.pin6, M4.D
  N60: SOCKET5_2.pin3, M5.A
  N61: SOCKET5_2.pin4, M5.C
  N62: SOCKET5_2.pin5, M5.B
  N63: SOCKET5_2.pin6, M5.D
  N64: SOCKET5_2.pin8, C5.+
